# Fritzing sketch sketch (saved by Fritzing 1.0.5)
breadboards: 1

parts:
  IR1 = vs1838b [package=THT]
  V1 = DC Power Supply [voltage=5V internal_resistance=1Ω max_current=0.1A]
  R1 = Resistor [tolerance=±5% resistance=220 package="2512 [SMD]"]
  R2 = Resistor [tolerance=±5% resistance=10k package="2512 [SMD]"]

nets:
  N1: IR1.GND, V1.Pin_1
  N2: IR1.Vs, R1.Pin_0, R2.Pin_1
  N3: IR1.Data, R2.Pin_0
  N4: V1.Pin_2, R1.Pin_1

notes:
  ロジックアナライザへ
  ロジックアナライザGNDへ
